# Fritzing sketch Sketch (saved by Fritzing 0.9.3b)
breadboards: 2

parts:
  Part1 = Arduino Uno (Rev3)
  LCD1 = LCD screen
  RE1 = Rotary Encoder [package=THT]
  Part2 = Ambient Light Sensor (TEMT6000 Breakout Board)
  R1 = PHOTOCELL [package=photocell]
  DHT1 = DHT11 Humitidy and Temperature Sensor
  R3 = Rotary Potentiometer (Small) [maximum_resistance=100kΩ package=THT]
  R4 = Resistor [tolerance=±5% resistance=1k package="0805 [SMD]"]
  R5 = Resistor [tolerance=±5% resistance=10k package="0805 [SMD]"]

nets:
  N1: Part1.A0, R1.P$2, R5.Pin_1
  N2: Part1.A1, Part2.S
  N3: Part1.D8, DHT1.DATA
  N4: Part1.D2, LCD1.DB7
  N5: Part1.D3_PWM, LCD1.DB6
  N6: Part1.D4, LCD1.DB5
  N7: Part1.D5_PWM, LCD1.DB4
  N8: Part1.D6_PWM, LCD1.RS
  N9: Part1.D7, LCD1.E
  VDD: Part1.5V, LCD1.VDD, RE1.SwitchrPinD, Part2.VCC, R1.P$1, DHT1.VDD, R3.leg1, R4.Pin_0
  GND: Part1.GND, LCD1.VSS, LCD1.R/W, LCD1.LED-, RE1.SwitchPinE, Part2.GND, DHT1.GND, R3.leg2, R5.Pin_0
  N10: LCD1.V0, R3.wiper
  N11: LCD1.LED+, R4.Pin_1

custom parts:
  Rotary Encoder: Rotary Encoder from ALPSec11e with switch.
  DHT11 Humitidy and Temperature Sensor: DHT11 Humidity and Temperature Sensor
